# Fritzing sketch PeltierWiring (saved by Fritzing 0.8.0b)
breadboards: 1

parts:
  J1 = Peltier Element  # not connected
  Part1 = Arduino Uno (Rev3)
  Q1 = Basic FET N-Channel [package="TO220 [THT]"]
  R1 = Resistor [tolerance=±20% resistance=10 package=THT]  # not connected

nets:
  N1: Part1.GND, Q1.source
